// Logisim project ex4.circ as structural Verilog: 5 circuits, main circuit RotRight
module RotRight (
  input  [15:0] INPUT0,
  input  [3:0] AMOUNT,
  output [15:0] OUTPUT0
);

  wire [15:0] rot1_1_out_2;

  rot1 rot1_1 (.in_1(INPUT0), .out_2(rot1_1_out_2));
  rot2 rot2_1 (.in_1(INPUT0), .out_2(rot1_1_out_2));
  rot4 rot4_1 (.in_1(INPUT0), .out_2(rot1_1_out_2));
  rot8 rot8_1 (.in_1(INPUT0), .out_2(rot1_1_out_2));
  Multiplexer #(.select(4), .width(16)) multiplexer_1 (
    .in1(rot1_1_out_2), .in2(rot1_1_out_2), .in3(rot1_1_out_2), .in4(rot1_1_out_2), .in5(rot1_1_out_2),
    .in6(rot1_1_out_2), .in7(rot1_1_out_2), .in8(rot1_1_out_2), .in9(rot1_1_out_2), .in10(rot1_1_out_2),
    .in11(rot1_1_out_2), .in12(rot1_1_out_2), .in13(rot1_1_out_2), .in14(rot1_1_out_2), .in15(rot1_1_out_2),
    .out(OUTPUT0), .sel(AMOUNT));  // open: in0
endmodule

module rot1 (
  input  [15:0] in_1,
  output [15:0] out_2
);


  assign out_2 = {in_1[0], in_1[15:1]};
endmodule

module rot2 (
  input  [15:0] in_1,
  output [15:0] out_2
);

  wire [15:0] rot1_1_out_2;

  rot1 rot1_1 (.in_1(in_1), .out_2(rot1_1_out_2));
  rot1 rot1_2 (.in_1(rot1_1_out_2), .out_2(out_2));
endmodule

module rot4 (
  input  [15:0] in_1,
  output [15:0] out_2
);

  wire [15:0] rot2_1_out_2;

  rot2 rot2_1 (.in_1(in_1), .out_2(rot2_1_out_2));
  rot2 rot2_2 (.in_1(rot2_1_out_2), .out_2(out_2));
endmodule

module rot8 (
  input  [15:0] in_1,
  output [15:0] out_2
);

  wire [15:0] rot4_1_out_2;

  rot4 rot4_1 (.in_1(in_1), .out_2(rot4_1_out_2));
  rot4 rot4_2 (.in_1(rot4_1_out_2), .out_2(out_2));
endmodule
